// Logisim project Trabalho SD.circ as structural Verilog: 4 circuits, main circuit main
module main (
);

  wire button_1_out, contador_1_a, contador_1_b, contador_1_c, contador_1_d, contador_1_e, contador_1_f,
       contador_1_g, or_1_out, \Semáforo_dos_Peões_amarelop , \Semáforo_dos_Peões_verdep ,
       \Semáforo_dos_Peões_vermelhop , \Semáforo_dos_Veículos_amarelov , \Semáforo_dos_Veículos_verdev ,
       \Semáforo_dos_Veículos_vermelhov ;

  Button button_1 (.out(button_1_out));
  \Semáforo_dos_Peões  \Semáforo_dos_Peões  (
    .SV____BP(button_1_out), .VermelhoP(\Semáforo_dos_Peões_vermelhop ),
    .AmareloP(\Semáforo_dos_Peões_amarelop ), .VerdeP(\Semáforo_dos_Peões_verdep ));
  \Semáforo_dos_Veículos  \Semáforo_dos_Veículos  (
    .SV____BP(button_1_out), .SSP(or_1_out), .VermelhoV(\Semáforo_dos_Veículos_vermelhov ),
    .AmareloV(\Semáforo_dos_Veículos_amarelov ), .VerdeV(\Semáforo_dos_Veículos_verdev ));
  or or_1 (or_1_out, \Semáforo_dos_Peões_verdep , \Semáforo_dos_Peões_amarelop );
  LED led_1 (.in(\Semáforo_dos_Veículos_vermelhov ));
  LED led_2 (.in(\Semáforo_dos_Veículos_amarelov ));
  LED led_3 (.in(\Semáforo_dos_Veículos_verdev ));
  LED led_4 (.in(\Semáforo_dos_Peões_vermelhop ));
  LED led_5 (.in(\Semáforo_dos_Peões_amarelop ));
  LED led_6 (.in(\Semáforo_dos_Peões_verdep ));
  Contador contador_1 (
    .SSP(\Semáforo_dos_Peões_verdep ), .a(contador_1_a), .b(contador_1_b), .c(contador_1_c),
    .d(contador_1_d), .e(contador_1_e), .f(contador_1_f), .g(contador_1_g));
  _7_Segment_Display u_7_segment_display_1 (
    .g(contador_1_g), .f(contador_1_f), .a(contador_1_a), .b(contador_1_b), .e(contador_1_e),
    .d(contador_1_d), .c(contador_1_c));  // open: dp

  // Notes on the sheet:
  //   SV || BP
  //   --------
  //   |
  //   |
  //   |
  //   |
  //   |
  //   |
  //   |
  //   |
  //   |
  //   |
  //   --------
  //   --------
  //   |
  //   |
  //   |
  //   |
  //   |
  //   |
  //   |
  //   |
  //   |
  //   |
  //   --------
endmodule

module \Semáforo_dos_Veículos  (
  input  SV____BP,
  input  SSP,
  output VermelhoV,
  output AmareloV,
  output VerdeV
);

  wire and_1_out, and_2_out, and_3_out, and_4_out, and_5_out, and_6_out, and_7_out, and_8_out, clock_1_out,
       not_1_out, or_1_out, or_2_out, X0_q, X0_qn, X1_q, X1_qn;

  Clock clock_1 (.out(clock_1_out));
  not not_1 (not_1_out, SSP);
  and and_1 (and_1_out, X1_qn, X0_q);
  and and_2 (and_2_out, not_1_out, X0_q);
  and and_3 (and_3_out, SV____BP, X1_qn);
  and and_4 (and_4_out, X0_q, X1_qn);
  and and_5 (and_5_out, not_1_out, X0_q);
  and and_6 (and_6_out, X1_q, X0_qn);
  or or_1 (or_1_out, and_1_out, and_2_out);
  or or_2 (or_2_out, and_3_out, and_4_out, and_5_out, and_6_out);
  T_Flip_Flop X1 (.clk(clock_1_out), .T(or_1_out), .Q(X1_q), .Qn(X1_qn));  // open: preset, reset, en
  T_Flip_Flop X0 (.clk(clock_1_out), .T(or_2_out), .Q(X0_q), .Qn(X0_qn));  // open: preset, reset, en
  and and_7 (and_7_out, X1_qn, X0_q);
  and and_8 (and_8_out, X1_q, X0_qn);
  and and_9 (VermelhoV, X1_q, X0_q);
  or or_3 (AmareloV, and_7_out, and_8_out);
  and and_10 (VerdeV, X1_qn, X0_qn);
endmodule

module Contador (
  input  SSP,
  output a,
  output b,
  output c,
  output d,
  output e,
  output f,
  output g
);

  wire and_1_out, and_2_out, and_3_out, and_4_out, and_5_out, and_6_out, and_7_out, and_8_out, and_9_out,
       and_10_out, and_11_out, and_12_out, and_13_out, and_14_out, and_15_out, and_16_out, and_17_out,
       and_18_out, and_19_out, and_20_out, and_21_out, and_22_out, and_23_out, and_24_out, and_25_out,
       and_26_out, and_27_out, and_28_out, and_29_out, and_30_out, and_31_out, and_32_out, and_33_out,
       and_34_out, and_35_out, and_36_out, and_37_out, and_38_out, and_39_out, and_40_out, and_41_out,
       and_42_out, and_43_out, and_44_out, and_45_out, and_46_out, and_47_out, and_48_out, and_49_out,
       and_50_out, and_51_out, and_52_out, clock_1_out, not_1_out, or_1_out, or_2_out, or_3_out, or_4_out,
       X0_q, X0_qn, X1_q, X1_qn, X2_q, X2_qn, X3_q, X3_qn;

  Clock clock_1 (.out(clock_1_out));
  not not_1 (not_1_out, SSP);
  and and_1 (and_1_out, X2_q, X1_q, X0_q, not_1_out);
  and and_2 (and_2_out, X3_q, not_1_out);
  and and_3 (and_3_out, X2_q, X1_q, X0_q, SSP);
  and and_4 (and_4_out, SSP, X3_q);
  and and_5 (and_5_out, X1_q, X0_q, not_1_out);
  and and_6 (and_6_out, X1_q, X0_q, SSP);
  and and_7 (and_7_out, X2_q, not_1_out);
  and and_8 (and_8_out, X0_q, X3_qn, not_1_out);
  and and_9 (and_9_out, X3_qn, X1_q, not_1_out);
  and and_10 (and_10_out, X3_qn, SSP);
  or or_1 (or_1_out, and_1_out, and_2_out, and_3_out, and_4_out);
  or or_2 (or_2_out, and_5_out, and_6_out);
  and and_11 (and_11_out, X0_q, not_1_out);
  or or_3 (or_3_out, and_11_out, and_12_out);
  and and_12 (and_12_out, SSP, X0_q);
  or or_4 (or_4_out, and_7_out, and_8_out, and_9_out, and_10_out);
  T_Flip_Flop X3 (.clk(clock_1_out), .T(or_1_out), .Q(X3_q), .Qn(X3_qn));  // open: preset, reset, en
  T_Flip_Flop X2 (.clk(clock_1_out), .T(or_2_out), .Q(X2_q), .Qn(X2_qn));  // open: preset, reset, en
  T_Flip_Flop X1 (.clk(clock_1_out), .T(or_3_out), .Q(X1_q), .Qn(X1_qn));  // open: preset, reset, en
  T_Flip_Flop X0 (.clk(clock_1_out), .T(or_4_out), .Q(X0_q), .Qn(X0_qn));  // open: preset, reset, en
  and and_13 (and_13_out, not_1_out, X3_qn, X0_qn);
  and and_14 (and_14_out, X1_q, not_1_out);
  and and_15 (and_15_out, X3_qn, not_1_out, X2_qn);
  and and_16 (and_16_out, SSP, X3_qn, X0_qn);
  and and_17 (and_17_out, X1_q, SSP);
  and and_18 (and_18_out, X3_qn, X2_qn, SSP);
  and and_19 (and_19_out, X2_qn, X1_qn, not_1_out);
  and and_20 (and_20_out, X2_q, X0_q, not_1_out);
  and and_21 (and_21_out, X1_q, X0_qn, not_1_out);
  and and_22 (and_22_out, X2_qn, X1_qn, SSP);
  and and_23 (and_23_out, X2_q, X0_q, SSP);
  and and_24 (and_24_out, X1_q, X0_qn, SSP);
  and and_25 (and_25_out, X3_qn, X1_qn, not_1_out);
  and and_26 (and_26_out, X3_qn, X2_qn, not_1_out);
  and and_27 (and_27_out, X3_q, not_1_out);
  and and_28 (and_28_out, X1_q, X0_qn, not_1_out);
  and and_29 (and_29_out, X3_qn, X1_qn, SSP);
  and and_30 (and_30_out, X3_qn, X2_qn, SSP);
  and and_31 (and_31_out, X3_q, SSP);
  and and_32 (and_32_out, X1_q, X0_qn, SSP);
  and and_33 (and_33_out, X3_qn, X2_qn, X1_qn, not_1_out);
  and and_34 (and_34_out, X3_qn, X2_q, X0_qn, not_1_out);
  and and_35 (and_35_out, X1_q, X0_q, not_1_out);
  and and_36 (and_36_out, X2_q, X1_q, not_1_out);
  and and_37 (and_37_out, X3_qn, X2_qn, X1_qn, SSP);
  and and_38 (and_38_out, X3_qn, X2_q, X0_qn, SSP);
  and and_39 (and_39_out, X1_q, X0_q, SSP);
  and and_40 (and_40_out, X2_q, X1_q, SSP);
  and and_41 (and_41_out, X3_qn, X2_qn, X1_qn, not_1_out);
  and and_42 (and_42_out, X1_q, X0_q, not_1_out);
  and and_43 (and_43_out, X1_q, X0_q, SSP);
  and and_44 (and_44_out, X3_qn, X2_qn, X1_qn, SSP);
  and and_45 (and_45_out, X3_qn, X1_qn, not_1_out);
  and and_46 (and_46_out, X2_qn, X1_q, X0_q, not_1_out);
  and and_47 (and_47_out, X3_qn, X1_qn, SSP);
  and and_48 (and_48_out, X2_qn, X1_q, X0_q, SSP);
  and and_49 (and_49_out, X2_q, not_1_out);
  and and_50 (and_50_out, X0_q, not_1_out);
  and and_51 (and_51_out, X2_q, SSP);
  and and_52 (and_52_out, X0_q, SSP);
  or or_5 (a, and_13_out, and_14_out, and_15_out, and_16_out, and_17_out, and_18_out);
  or or_6 (b, and_19_out, and_20_out, and_21_out, and_22_out, and_23_out, and_24_out);
  or or_7 (c, and_25_out, and_26_out, and_27_out, and_28_out, and_29_out, and_30_out, and_31_out, and_32_out);
  or or_8 (d, and_33_out, and_34_out, and_35_out, and_36_out, and_37_out, and_38_out, and_39_out, and_40_out);
  or or_9 (e, and_41_out, and_42_out, and_43_out, and_44_out);
  or or_10 (f, and_45_out, and_46_out, and_47_out, and_48_out);
  or or_11 (g, and_49_out, and_50_out, and_51_out, and_52_out);
endmodule

// T0
module \Semáforo_dos_Peões  (
  input  SV____BP,
  output VermelhoP,
  output AmareloP,
  output VerdeP
);

  wire and_1_out, and_2_out, and_3_out, and_4_out, and_5_out, and_6_out, and_7_out, and_8_out, and_9_out,
       and_10_out, and_11_out, and_12_out, and_13_out, and_14_out, and_15_out, and_16_out, and_17_out,
       and_18_out, and_19_out, and_20_out, and_21_out, and_22_out, and_23_out, and_24_out, and_25_out,
       and_26_out, and_27_out, and_28_out, and_29_out, and_30_out, and_31_out, and_32_out, and_33_out,
       and_34_out, clock_1_out, not_1_out, or_1_out, or_2_out, or_3_out, or_4_out, T0_q, T0_qn, T1_q, T1_qn,
       T2_q, T2_qn, T3_q, T3_qn;

  Clock clock_1 (.out(clock_1_out));
  not not_1 (not_1_out, SV____BP);
  and and_1 (and_1_out, T3_q, T2_q, T0_q, not_1_out);
  and and_2 (and_2_out, T2_q, T1_q, T0_q, not_1_out);
  and and_3 (and_3_out, T3_q, T2_q, T0_q, SV____BP);
  and and_4 (and_4_out, T2_q, T1_q, T0_q, SV____BP);
  and and_5 (and_5_out, T3_q, T2_q, T0_q, not_1_out);
  and and_6 (and_6_out, T1_q, T0_q, not_1_out);
  and and_7 (and_7_out, T3_q, T2_q, T0_q, SV____BP);
  and and_8 (and_8_out, T1_q, T0_q, SV____BP);
  and and_9 (and_9_out, T3_qn, T0_q, not_1_out);
  and and_10 (and_10_out, T2_qn, T0_q, not_1_out);
  and and_11 (and_11_out, T3_qn, T0_q, SV____BP);
  and and_12 (and_12_out, T2_qn, T0_q, SV____BP);
  and and_13 (and_13_out, T0_q, not_1_out);
  and and_14 (and_14_out, T1_q, not_1_out);
  and and_15 (and_15_out, T2_q, not_1_out);
  and and_16 (and_16_out, T3_q, not_1_out);
  or or_1 (or_1_out, and_1_out, and_2_out, and_3_out, and_4_out);
  or or_2 (or_2_out, and_5_out, and_6_out, and_7_out, and_8_out);
  or or_3 (or_3_out, and_9_out, and_10_out, and_11_out, and_12_out);
  or or_4 (or_4_out, and_13_out, and_14_out, and_15_out, and_16_out, SV____BP);
  T_Flip_Flop T3 (.clk(clock_1_out), .T(or_1_out), .Q(T3_q), .Qn(T3_qn));  // open: preset, reset, en
  T_Flip_Flop T2 (.clk(clock_1_out), .T(or_2_out), .Q(T2_q), .Qn(T2_qn));  // open: preset, reset, en
  T_Flip_Flop T1 (.clk(clock_1_out), .T(or_3_out), .Q(T1_q), .Qn(T1_qn));  // open: preset, reset, en
  T_Flip_Flop T0 (.clk(clock_1_out), .T(or_4_out), .Q(T0_q), .Qn(T0_qn));  // open: preset, reset, en
  and and_17 (and_17_out, T3_qn, T2_qn, T0_qn, not_1_out);
  and and_18 (and_18_out, T3_qn, T2_qn, T1_qn, not_1_out);
  and and_19 (and_19_out, T3_q, T2_q, T0_q, not_1_out);
  and and_20 (and_20_out, T3_qn, T2_qn, T0_qn, SV____BP);
  and and_21 (and_21_out, T3_qn, T2_qn, T1_qn, SV____BP);
  and and_22 (and_22_out, T3_q, T2_q, T0_q, SV____BP);
  and and_23 (and_23_out, T3_q, T2_q, T0_qn, not_1_out);
  and and_24 (and_24_out, T3_q, T1_q, T0_q, not_1_out);
  and and_25 (and_25_out, T3_q, T2_q, T0_qn, SV____BP);
  and and_26 (and_26_out, T3_q, T0_q, T1_q, SV____BP);
  and and_27 (and_27_out, T3_qn, T1_q, T0_q, not_1_out);
  and and_28 (and_28_out, T3_qn, T2_q, not_1_out);
  and and_29 (and_29_out, T3_q, T2_qn, T1_qn, not_1_out);
  and and_30 (and_30_out, T3_q, T1_q, T0_qn, not_1_out);
  and and_31 (and_31_out, T3_qn, T1_q, T0_q, SV____BP);
  and and_32 (and_32_out, T3_qn, T2_qn, T2_q);
  and and_33 (and_33_out, T3_q, T2_qn, T1_qn, SV____BP);
  and and_34 (and_34_out, T3_q, T1_q, T0_qn, SV____BP);
  or or_5 (VermelhoP, and_17_out, and_18_out, and_19_out, and_20_out, and_21_out, and_22_out);
  or or_6 (AmareloP, and_23_out, and_24_out, and_25_out, and_26_out);
  or or_7 (VerdeP, and_27_out, and_28_out, and_29_out, and_30_out, and_31_out, and_32_out, and_33_out, and_34_out);

  // Notes on the sheet:
  //   --------
  //   |
  //   |
  //   |
  //   |
  //   |
  //   |
  //   |
  //   |
  //   |
  //   --------
endmodule
